// Logisim project Simplz.circ as structural Verilog: 6 circuits, main circuit main
module main (
  input  [7:0] INPUT,
  output [7:0] OUTPUT
);

  wire alu_1_carry, and_1_out, carry_latch_1_out, control_1_accum_carry_clk, control_1_alu_mode,
       control_1_carry_clear, control_1_i___pc_to_mem, control_1_instruction_clock, control_1_mem_write,
       control_1_pc_clk, control_1_pc_load, not_1_out, not_2_out, not_3_out, not_4_out, not_5_out, Reset_out,
       simple_memory_1_read_input, simple_memory_1_write_output;
  wire [5:0] controlled_buffer_3_out, PC_q;
  wire [7:0] accum_2_out_3, accum_3_out_3, alu_1_out, controlled_buffer_1_out;

  assign controlled_buffer_1_out = simple_memory_1_read_input ? INPUT : 8'bz;  // Controlled_Buffer controlled_buffer_1
  Simple_Memory simple_memory_1 (
    .WRITE_OUTPUT(simple_memory_1_write_output), .READ_INPUT(simple_memory_1_read_input),
    .MEMORY_READ(control_1_mem_write), .out_4(controlled_buffer_1_out), .in_2(controlled_buffer_1_out),
    .in_3(controlled_buffer_3_out));
  Accum accum_1 (.in_1(controlled_buffer_1_out), .out_3(OUTPUT), .Clk(simple_memory_1_write_output));
  ALU alu_1 (
    .A(accum_2_out_3), .B(controlled_buffer_1_out), .Out(alu_1_out), .Carry(alu_1_carry),
    .Mode(control_1_alu_mode));
  Accum accum_2 (.in_1(alu_1_out), .out_3(accum_2_out_3), .Clk(control_1_accum_carry_clk));
  Pull_Resistor pull_resistor_1 (.node(controlled_buffer_1_out));
  Carry_Latch carry_latch_1 (
    .Dat(alu_1_carry), .Clk(and_1_out), .Out(carry_latch_1_out), .Carry_Clear(control_1_carry_clear));
  not not_1 (not_1_out, control_1_alu_mode);
  and and_1 (and_1_out, not_1_out, control_1_accum_carry_clk);
  not not_2 (not_2_out, control_1_mem_write);
  Control control_1 (
    .Carry_Clear(control_1_carry_clear), .Carry_State(carry_latch_1_out), .ALU_Mode(control_1_alu_mode),
    .Mem_Write(control_1_mem_write), .Instruction_Clock(control_1_instruction_clock),
    .Accum_Carry_Clk(control_1_accum_carry_clk), .I___PC_to_mem(control_1_i___pc_to_mem),
    .PC_Clk(control_1_pc_clk), .Reset(Reset_out), .PC_load(control_1_pc_load), .in_1(accum_3_out_3));  // open: MEM_READ_ARG
  assign controlled_buffer_1_out = not_2_out ? accum_2_out_3 : 8'bz;  // Controlled_Buffer controlled_buffer_2
  Accum accum_3 (.in_1(controlled_buffer_1_out), .out_3(accum_3_out_3), .Clk(control_1_instruction_clock));
  not not_3 (not_3_out, control_1_pc_load);
  not not_4 (not_4_out, control_1_i___pc_to_mem);
  assign controlled_buffer_3_out = not_4_out ? accum_3_out_3[5:0] : 6'bz;  // Controlled_Buffer controlled_buffer_3
  assign controlled_buffer_3_out = control_1_i___pc_to_mem ? PC_q : 6'bz;  // Controlled_Buffer controlled_buffer_4
  not not_5 (not_5_out, not_3_out);
  Button Reset (.out(Reset_out));
  Counter #(.width(6), .max('h3f)) PC (
    .load(not_5_out), .D(accum_3_out_3[5:0]), .count(not_3_out), .Q(PC_q), .clk(control_1_pc_clk), .clr(1'b0));  // open: carry
endmodule

module ALU (
  input  [7:0] A,
  input  [7:0] B,
  input  Mode,
  output Carry,
  output [7:0] Out
);

  wire not_1_out, not_2_out;
  wire [7:0] adder_1_out, nor_1_out;

  Adder adder_1 (.a(B), .b(A), .out(adder_1_out), .cin(1'b0), .cout(Carry));
  assign nor_1_out = ~(B | A);  // NOR_Gate nor_1, 8 bits wide
  assign Out = not_2_out ? adder_1_out : 8'bz;  // Controlled_Buffer controlled_buffer_1
  assign Out = not_1_out ? nor_1_out : 8'bz;  // Controlled_Buffer controlled_buffer_2
  not not_1 (not_1_out, not_2_out);
  not not_2 (not_2_out, Mode);
endmodule

// Register
module Accum (
  input  [7:0] in_1,
  input  Clk,
  output [7:0] out_3
);

  Register register_1 (.D(in_1), .en(1'b1), .Q(out_3), .clk(Clk), .clr(1'b0));
endmodule

// C
module Carry_Latch (
  input  Clk,
  input  Dat,
  input  Carry_Clear,
  output Out
);

  D_Flip_Flop d_ff_1 (.clk(Clk), .D(Dat), .Q(Out), .preset(1'b0), .en(1'b1), .reset(Carry_Clear));  // open: Qn
endmodule

module Control (
  input  [7:0] in_1,
  input  Carry_State,
  input  Reset,
  output Instruction_Clock,
  output Carry_Clear,
  output ALU_Mode,
  output Accum_Carry_Clk,
  output I___PC_to_mem,
  output PC_Clk,
  output PC_load,
  output Mem_Write,
  output MEM_READ_ARG
);

  wire button_1_out, clock_1_out, decoder_1_out0, decoder_1_out2, decoder_1_out5, decoder_1_out6, not_1_out,
       not_2_out, not_4_out, not_5_out, or_4_out;
  wire [0:0] controlled_buffer_3_out, xor_1_out;
  wire [1:0] controlled_buffer_1_out, register_1_q;

  Clock clock_1 (.out(clock_1_out));
  Button button_1 (.out(button_1_out));
  xor xor_1 (xor_1_out[0], clock_1_out, button_1_out);
  not not_1 (not_1_out, Carry_State);
  not not_2 (not_2_out, xor_1_out[0]);
  not not_3 (Mem_Write, decoder_1_out5);
  Register #(.width(2)) register_1 (
    .D(controlled_buffer_1_out), .en(1'b1), .Q(register_1_q), .clk(not_2_out), .clr(Reset));
  Decoder #(.select(3), .enable("false")) decoder_1 (
    .out0(decoder_1_out0), .out1(Instruction_Clock), .out2(decoder_1_out2), .out3(Accum_Carry_Clk),
    .out5(decoder_1_out5), .out6(decoder_1_out6), .out7(Carry_Clear), .sel({register_1_q, xor_1_out[0]}));  // open: out4
  or or_1 (MEM_READ_ARG, Accum_Carry_Clk, decoder_1_out2);
  or or_2 (I___PC_to_mem, decoder_1_out0, Instruction_Clock);
  assign controlled_buffer_1_out = not_4_out ? 2'b00 : 2'bz;  // Controlled_Buffer controlled_buffer_1
  not not_4 (not_4_out, Instruction_Clock);
  or or_3 (PC_Clk, Carry_Clear, decoder_1_out5, Accum_Carry_Clk);
  assign controlled_buffer_1_out = Instruction_Clock ? {in_1[7], controlled_buffer_3_out[0]} : 2'bz;  // Controlled_Buffer controlled_buffer_2
  or or_4 (or_4_out, decoder_1_out6, Carry_Clear);
  assign controlled_buffer_3_out[0] = in_1[7] ? in_1[6] : 1'bz;  // Controlled_Buffer controlled_buffer_3
  and and_1 (PC_load, not_1_out, or_4_out);
  assign controlled_buffer_3_out[0] = not_5_out ? 1'b1 : 1'bz;  // Controlled_Buffer controlled_buffer_4
  not not_5 (not_5_out, in_1[7]);

  assign ALU_Mode = in_1[6];
endmodule

module Simple_Memory (
  input  MEMORY_READ,
  input  [7:0] in_2,
  input  [5:0] in_3,
  output [7:0] out_4,
  output WRITE_OUTPUT,
  output READ_INPUT
);

  wire and_3_out, not_1_out, not_2_out;
  wire [7:0] ram_1_data;

  and and_1 (WRITE_OUTPUT, in_3[0], ~MEMORY_READ, and_3_out);  // AND_Gate
  and and_2 (READ_INPUT, ~in_3[0], and_3_out);  // AND_Gate
  RAM #(.addrWidth(6), .bus("asynch")) ram_1 (
    .addr(in_3), .data(ram_1_data), .sel(not_1_out), .ld(MEMORY_READ), .clr(1'b0));
  and and_3 (and_3_out, in_3[1], in_3[2], in_3[3], in_3[4], in_3[5]);
  not not_1 (not_1_out, and_3_out);
  assign out_4 = MEMORY_READ ? ram_1_data : 8'bz;  // Controlled_Buffer controlled_buffer_1
  not not_2 (not_2_out, MEMORY_READ);
  assign ram_1_data = not_2_out ? in_2 : 8'bz;  // Controlled_Buffer controlled_buffer_2
endmodule
